# Fritzing sketch esquema_robson (saved by Fritzing 0.9.3b)
circuit board: 6.92514cm x 5.59517cm
breadboards: 1

parts:
  DHT1 = DHT11 Humitidy and Temperature Sensor
  R1 = Resistor [tolerance=±5% resistance=220 package=THT]
  LED2 = LEDs [package=led10mm]
  Componente1 = Arduino Uno (Rev3) - ICSP
  IR1 = TSOP312.., 314.. [package=THT]

nets:
  VDD: DHT1.VDD, Componente1.5V, IR1.Vs
  N1: DHT1.DATA, Componente1.A1
  GND: DHT1.GND, LED2.C, Componente1.GND, IR1.GND
  N2: R1.Pin_0, LED2.A
  N3: R1.Pin_1, Componente1.D5_PWM
  N4: Componente1.D3_PWM, IR1.Data

custom parts:
  DHT11 Humitidy and Temperature Sensor: DHT11 Humidity and Temperature Sensor
